// Logisim project hiasat.circ as structural Verilog
module main (
  input  in_1,
  input  in_2,
  input  in_3,
  input  in_4,
  input  in_5,
  input  in_6,
  input  in_7,
  input  in_8,
  input  in_9,
  input  in_10,
  input  in_11,
  input  in_12,
  input  in_13,
  input  in_14,
  input  in_15,
  input  in_16,
  input  in_17,
  input  in_18,
  input  in_19,
  input  in_20,
  input  in_21,
  output out_22,
  output out_23,
  output out_24,
  output out_25,
  output out_26,
  output out_27,
  output out_28
);

  wire ap0, ap1, ap2, ap3, ap4, ap5, ap6, bp1, bp2, bp3, bp4, bp5, bp6, bp7, cout, delay1_1_ogi,
       delay1_1_ogpi, delay1_1_opi, delay1_1_oppi, delay1_3_ogi, delay1_3_ogpi, delay1_3_opi, delay1_3_oppi,
       delay1_5_ogi, delay1_5_ogpi, delay1_5_opi, delay1_5_oppi, delay1_6_ogi, delay1_6_ogpi, delay1_6_opi,
       delay1_6_oppi, dg0, dg01, dg2, dg4, dg6, dg012, dg45, dg0123, dgp0, dgp01, dgp2, dgp4, dgp6, dgp012,
       dgp45, dgp0123, dp0, dp01, dp2, dp4, dp6, dp012, dp45, dp0123, dpp0, dpp01, dpp2, dpp4, dpp6, dpp012,
       dpp45, dpp0123, g0, g01, g1, g2, g3, g4, g5, g6, g012, g23, g45, g0123, g456, g01234, g012345,
       g0123456, gp0, gp01, gp1, gp2, gp3, gp4, gp5, gp6, gp012, gp23, gp45, gp0123, gp456, gp01234,
       gp012345, gp0123456, h0, h1, h2, h3, h4, h5, h6, hp0, hp1, hp2, hp3, hp4, hp5, hp6, multiplexer_3_out,
       multiplexer_4_out, multiplexer_5_out, multiplexer_6_out, multiplexer_7_out, multiplexer_8_out,
       multiplexer_9_out, multiplexer_10_out, multiplexer_11_out, multiplexer_12_out, multiplexer_13_out,
       multiplexer_14_out, p0, p01, p1, p2, p3, p4, p5, p6, p012, p23, p45, p0123, p456, p01234, p012345,
       p0123456, pp0, pp01, pp1, pp2, pp3, pp4, pp5, pp6, pp012, pp23, pp45, pp0123, pp456, pp01234,
       pp012345, pp0123456, undriven;

  Hashed_cell hashed_cell_1 (.bi(in_21), .ai(in_7), .ki(in_14), .gi(g0), .hi(h0), .pi(p0), .api(ap0), .bpi1(bp1));
  Hashed_cell hashed_cell_2 (.bi(in_20), .ai(in_6), .ki(in_13), .gi(g1), .hi(h1), .pi(p1), .api(ap1), .bpi1(bp2));
  Hashed_cell hashed_cell_3 (.bi(in_19), .ai(in_5), .ki(in_12), .gi(g2), .hi(h2), .pi(p2), .api(ap2), .bpi1(bp3));
  Hashed_cell hashed_cell_4 (.bi(in_18), .ai(in_4), .ki(in_11), .gi(g3), .hi(h3), .pi(p3), .api(ap3), .bpi1(bp4));
  Hashed_cell hashed_cell_5 (.bi(in_17), .ai(in_3), .ki(in_10), .gi(g4), .hi(h4), .pi(p4), .api(ap4), .bpi1(bp5));
  Hashed_cell hashed_cell_6 (.bi(in_16), .ai(in_2), .ki(in_9), .gi(g5), .hi(h5), .pi(p5), .api(ap5), .bpi1(bp6));
  Hashed_cell hashed_cell_7 (.bi(in_15), .ai(in_1), .ki(in_8), .gi(g6), .hi(h6), .pi(p6), .api(ap6), .bpi1(bp7));
  // NoConnect on undriven
  Envelope_cell envelope_cell_1 (.bpi(undriven), .api(ap0), .ppi(pp0), .hpi(hp0), .gpi(gp0));
  Envelope_cell envelope_cell_2 (.bpi(bp1), .api(ap1), .ppi(pp1), .hpi(hp1), .gpi(gp1));
  Envelope_cell envelope_cell_3 (.bpi(bp2), .api(ap2), .ppi(pp2), .hpi(hp2), .gpi(gp2));
  Envelope_cell envelope_cell_4 (.bpi(bp3), .api(ap3), .ppi(pp3), .hpi(hp3), .gpi(gp3));
  Envelope_cell envelope_cell_5 (.bpi(bp4), .api(ap4), .ppi(pp4), .hpi(hp4), .gpi(gp4));
  Envelope_cell envelope_cell_6 (.bpi(bp5), .api(ap5), .ppi(pp5), .hpi(hp5), .gpi(gp5));
  Envelope_cell envelope_cell_7 (.bpi(bp6), .api(ap6), .ppi(pp6), .hpi(hp6), .gpi(gp6));
  Delay1 delay1_1 (
    .pi(p0), .gi(g0), .ppi(pp0), .gpi(gp0), .opi(delay1_1_opi), .ogi(delay1_1_ogi), .oppi(delay1_1_oppi),
    .ogpi(delay1_1_ogpi));
  Black_node black_node_1 (.pim1(p0), .pi(p1), .gim1(g0), .gi(g1), .piim1(p01), .giim1(g01));
  Black_node black_node_2 (.pim1(pp0), .pi(pp1), .gim1(gp0), .gi(gp1), .piim1(pp01), .giim1(gp01));
  Delay1 delay1_2 (.pi(p2), .gi(g2), .ppi(pp2), .gpi(gp2), .opi(dp2), .ogi(dg2), .oppi(dpp2), .ogpi(dgp2));
  Black_node black_node_3 (.pim1(p2), .pi(p3), .gim1(g2), .gi(g3), .piim1(p23), .giim1(g23));
  Black_node black_node_4 (.pim1(pp2), .pi(pp3), .gim1(gp2), .gi(gp3), .piim1(pp23), .giim1(gp23));
  Delay1 delay1_3 (
    .pi(p4), .gi(g4), .ppi(pp4), .gpi(gp4), .opi(delay1_3_opi), .ogi(delay1_3_ogi), .oppi(delay1_3_oppi),
    .ogpi(delay1_3_ogpi));
  Black_node black_node_5 (.pim1(p4), .pi(p5), .gim1(g4), .gi(g5), .piim1(p45), .giim1(g45));
  Black_node black_node_6 (.pim1(pp4), .pi(pp5), .gim1(gp4), .gi(gp5), .piim1(pp45), .giim1(gp45));
  Delay1 delay1_4 (.pi(p6), .gi(g6), .ppi(pp6), .gpi(gp6), .opi(dp6), .ogi(dg6), .oppi(dpp6), .ogpi(dgp6));
  Delay1 delay1_5 (
    .pi(delay1_1_opi), .gi(delay1_1_ogi), .ppi(delay1_1_oppi), .gpi(delay1_1_ogpi), .opi(delay1_5_opi),
    .ogi(delay1_5_ogi), .oppi(delay1_5_oppi), .ogpi(delay1_5_ogpi));
  Delay1 delay1_6 (
    .pi(p01), .gi(g01), .ppi(pp01), .gpi(gp01), .opi(delay1_6_opi), .ogi(delay1_6_ogi), .oppi(delay1_6_oppi),
    .ogpi(delay1_6_ogpi));
  Black_node black_node_7 (.pim1(p01), .pi(dp2), .gim1(g01), .gi(dg2), .piim1(p012), .giim1(g012));
  Black_node black_node_8 (.pim1(pp01), .pi(dpp2), .gim1(gp01), .gi(dgp2), .piim1(pp012), .giim1(gp012));
  Black_node black_node_9 (.pim1(p01), .pi(p23), .gim1(g01), .gi(g23), .piim1(p0123), .giim1(g0123));
  Black_node black_node_10 (.pim1(pp01), .pi(pp23), .gim1(gp01), .gi(gp23), .piim1(pp0123), .giim1(gp0123));
  Delay1 delay1_7 (
    .pi(delay1_3_opi), .gi(delay1_3_ogi), .ppi(delay1_3_oppi), .gpi(delay1_3_ogpi), .opi(dp4), .ogi(dg4),
    .oppi(dpp4), .ogpi(dgp4));
  Delay1 delay1_8 (.pi(p45), .gi(g45), .ppi(pp45), .gpi(gp45), .opi(dp45), .ogi(dg45), .oppi(dpp45), .ogpi(dgp45));
  Black_node black_node_11 (.pim1(p45), .pi(dp6), .gim1(g45), .gi(dg6), .piim1(p456), .giim1(g456));
  Black_node black_node_12 (.pim1(pp45), .pi(dpp6), .gim1(gp45), .gi(dgp6), .piim1(pp456), .giim1(gp456));
  Delay1 delay1_9 (
    .pi(delay1_5_opi), .gi(delay1_5_ogi), .ppi(delay1_5_oppi), .gpi(delay1_5_ogpi), .opi(dp0), .ogi(dg0),
    .oppi(dpp0), .ogpi(dgp0));
  Delay1 delay1_10 (
    .pi(delay1_6_opi), .gi(delay1_6_ogi), .ppi(delay1_6_oppi), .gpi(delay1_6_ogpi), .opi(dp01), .ogi(dg01),
    .oppi(dpp01), .ogpi(dgp01));
  Delay1 delay1_11 (
    .pi(p012), .gi(g012), .ppi(pp012), .gpi(gp012), .opi(dp012), .ogi(dg012), .oppi(dpp012), .ogpi(dgp012));
  Delay1 delay1_12 (
    .pi(p0123), .gi(g0123), .ppi(pp0123), .gpi(gp0123), .opi(dp0123), .ogi(dg0123), .oppi(dpp0123),
    .ogpi(dgp0123));
  Black_node black_node_13 (.pim1(p0123), .pi(dp4), .gim1(g0123), .gi(dg4), .piim1(p01234), .giim1(g01234));
  Black_node black_node_14 (.pim1(pp0123), .pi(dpp4), .gim1(gp0123), .gi(dgp4), .piim1(pp01234), .giim1(gp01234));
  Black_node black_node_15 (.pim1(p0123), .pi(dp45), .gim1(g0123), .gi(dg45), .piim1(p012345), .giim1(g012345));
  Black_node black_node_16 (.pim1(pp0123), .pi(dpp45), .gim1(gp0123), .gi(dgp45), .piim1(pp012345), .giim1(gp012345));
  Black_node black_node_17 (.pim1(p0123), .pi(p456), .gim1(g0123), .gi(g456), .piim1(p0123456), .giim1(g0123456));
  Black_node black_node_18 (.pim1(pp0123), .pi(pp456), .gim1(gp0123), .gi(gp456), .piim1(pp0123456), .giim1(gp0123456));
  Multiplexer multiplexer_1 (.in0(gp0123456), .in1(g0123456), .out(cout), .sel(bp7));
  Multiplexer multiplexer_2 (.in0(h0), .in1(hp0), .out(out_28), .sel(cout));
  Multiplexer multiplexer_3 (.in0(dg0), .in1(dgp0), .out(multiplexer_3_out), .sel(cout));
  Multiplexer multiplexer_4 (.in0(h1), .in1(hp1), .out(multiplexer_4_out), .sel(cout));
  Multiplexer multiplexer_5 (.in0(dg01), .in1(dgp01), .out(multiplexer_5_out), .sel(cout));
  Multiplexer multiplexer_6 (.in0(h2), .in1(hp2), .out(multiplexer_6_out), .sel(cout));
  Multiplexer multiplexer_7 (.in0(dg012), .in1(dgp012), .out(multiplexer_7_out), .sel(cout));
  Multiplexer multiplexer_8 (.in0(h3), .in1(hp3), .out(multiplexer_8_out), .sel(cout));
  Multiplexer multiplexer_9 (.in0(dg0123), .in1(dgp0123), .out(multiplexer_9_out), .sel(cout));
  Multiplexer multiplexer_10 (.in0(h4), .in1(hp4), .out(multiplexer_10_out), .sel(cout));
  Multiplexer multiplexer_11 (.in0(g01234), .in1(gp01234), .out(multiplexer_11_out), .sel(cout));
  Multiplexer multiplexer_12 (.in0(h5), .in1(hp5), .out(multiplexer_12_out), .sel(cout));
  Multiplexer multiplexer_13 (.in0(g012345), .in1(gp012345), .out(multiplexer_13_out), .sel(cout));
  Multiplexer multiplexer_14 (.in0(h6), .in1(hp6), .out(multiplexer_14_out), .sel(cout));
  xor xor_1 (out_27, multiplexer_3_out, multiplexer_4_out);
  xor xor_2 (out_26, multiplexer_5_out, multiplexer_6_out);
  xor xor_3 (out_25, multiplexer_7_out, multiplexer_8_out);
  xor xor_4 (out_24, multiplexer_9_out, multiplexer_10_out);
  xor xor_5 (out_23, multiplexer_11_out, multiplexer_12_out);
  xor xor_6 (out_22, multiplexer_13_out, multiplexer_14_out);

  // Other names for the same wires on the sheet: a0 = in_7; a1 = in_6; a2 = in_5; a3 = in_4; a4 = in_3; a5 = in_2;
  //   a6 = in_1; b0 = in_21; b1 = in_20; b2 = in_19; b3 = in_18; b4 = in_17; b5 = in_16; b6 = in_15; k0 = in_14;
  //   k1 = in_13; k2 = in_12; k3 = in_11; k4 = in_10; k5 = in_9; k6 = in_8; s0 = out_28; s1 = out_27; s2 = out_26;
  //   s3 = out_25; s4 = out_24; s5 = out_23; s6 = out_22
endmodule

module Hashed_cell (
  input  bi,
  input  ai,
  input  ki,
  output gi,
  output hi,
  output pi,
  output api,
  output bpi1
);

  wire not_1_out;

  or or_1 (pi, bi, ai);
  and and_1 (gi, bi, ai);
  and and_2 (hi, pi, ~gi);  // AND_Gate
  Multiplexer multiplexer_1 (.in0(hi), .in1(not_1_out), .out(api), .sel(ki));
  not not_1 (not_1_out, hi);
  Multiplexer multiplexer_2 (.in0(gi), .in1(pi), .out(bpi1), .sel(ki));
endmodule

module Envelope_cell (
  input  bpi,
  input  api,
  output ppi,
  output hpi,
  output gpi
);

  or or_1 (ppi, bpi, api);
  and and_1 (gpi, bpi, api);
  and and_2 (hpi, ppi, ~gpi);  // AND_Gate
endmodule

module Black_node (
  input  pim1,
  input  pi,
  input  gim1,
  input  gi,
  output piim1,
  output giim1
);

  wire and_2_out;

  and and_1 (piim1, pim1, pi);
  and and_2 (and_2_out, pi, gim1);
  or or_1 (giim1, and_2_out, gi);
endmodule

module Delay1 (
  input  pi,
  input  gi,
  input  ppi,
  input  gpi,
  output opi,
  output ogi,
  output oppi,
  output ogpi
);

  buf buffer_1 (opi, pi);
  buf buffer_2 (ogi, gi);
  buf buffer_3 (oppi, ppi);
  buf buffer_4 (ogpi, gpi);
endmodule
